// Logisim project cpu.circ as structural Verilog: 1 circuit, main circuit cpu
module cpu (
  input  clk,
  input  [31:0] INSTRUCTION,
  input  [31:0] READ_DATA,
  output [31:0] WRITE_ADDRESS,
  output [31:0] PROGRAM_COUNTER,
  output [31:0] ra,
  output [31:0] sp,
  output [31:0] t0,
  output [31:0] t1,
  output [31:0] t2,
  output [31:0] s0,
  output [31:0] s1,
  output [31:0] a0,
  output [31:0] tohost,
  output [3:0] WRITE_ENABLE,
  output [31:0] WRITE_DATA
);

  wire ASel, BSel, RegWen;
  wire [1:0] WBSel;
  wire [3:0] ALUSel;
  wire [31:0] adder_1_out, alu_1_result, dataD, imme, INSTRUCTION_R, multiplexer_1_out, multiplexer_2_out,
       READ_DATA1, READ_DATA2;

  Adder #(.width(32)) adder_1 (.a(PROGRAM_COUNTER), .b(32'h4), .out(adder_1_out));  // open: cin, cout
  Register #(.width(32)) PC (.D(adder_1_out), .clk(clk), .Q(PROGRAM_COUNTER));  // open: en, clr
  control_logic control_logic_1 (
    .RegWEn(RegWen), .ASel(ASel), .BSel(BSel), .ALUSel(ALUSel), .WBSel(WBSel), .inst(INSTRUCTION_R));  // open: CSRWen, PCSel, ImmSel, BrUn, MemRW, CSRSel, BrEq, BrLt
  imm_gen imm_gen_1 (.inst(INSTRUCTION_R), .imm(imme));  // open: ImmSel
  Register #(.width(32)) register_1 (.D(INSTRUCTION), .clk(clk), .Q(INSTRUCTION_R));  // open: en, clr
  regfile regfile_1 (
    .rs1(INSTRUCTION_R[19:15]), .rs2(INSTRUCTION_R[24:20]), .rd(INSTRUCTION_R[11:7]), .Write_Data(dataD),
    .RegWEn(RegWen), .clk(clk), .ra(ra), .sp(sp), .t0(t0), .t1(t1), .t2(t2), .s0(s0), .s1(s1), .a0(a0),
    .Read_Data_1(READ_DATA1), .Read_Data_2(READ_DATA2));
  // branch_comp branch_comp_1: pin names not known
  Multiplexer #(.enable("false"), .width(32)) multiplexer_1 (
    .in0(READ_DATA1), .out(multiplexer_1_out), .sel(ASel));  // open: in1
  Multiplexer #(.enable("false"), .width(32)) multiplexer_2 (
    .in0(READ_DATA2), .in1(imme), .out(multiplexer_2_out), .sel(BSel));
  csr csr_1 (.tohost(tohost));  // open: CSR_address, CSR_din, CSR_WE, clk
  alu alu_1 (.Result(alu_1_result), .A(multiplexer_1_out), .B(multiplexer_2_out), .ALUSel(ALUSel));
  Multiplexer #(.enable("false"), .select(2), .width(32)) multiplexer_3 (
    .in0(READ_DATA), .in1(alu_1_result), .out(dataD), .sel(WBSel));  // open: in2, in3

  // Notes on the sheet:
  //   Output to IMEM
  //   IMEM (do **NOT** move this)
  //   Inputs from IMEM
  //   It is OK to move the PC, RegFile, ALU, MEM, Branch Comp, Imm Gen, and Control Logic to wherever is most convenient for you when constructing your CPU, and to delete this text
  //   Inputs/Outputs for testing. Do **NOT** move these.
  //   Outputs To DMEM
  //   DMEM (do **NOT** move this)
  //   Inputs From DMEM
endmodule
